// Logisim project ALU.circ as structural Verilog: 1 circuit, main circuit Ida ALU
// ALU
module Ida_ALU (
  input  [23:0] ALU_Source_1,
  input  [23:0] ALU_Source_2,
  input  [3:0] Operation,
  output [23:0] ALU_Result
);

  wire [1:0] sign_comp, unsign_comp;
  wire [4:0] bit_extender_1_out, bit_extender_2_out, bit_extender_3_out, bit_extender_4_out,
       bit_extender_5_out;
  wire [23:0] add, \and , ior, rl, rr, sll, sra, srl, srr, subt, \xor ;

  // Probe on ALU_Source_1
  // Probe on ALU_Source_2
  // Probe on Operation
  // Probe on ALU_Result
  Multiplexer #(.select(4), .width(24), .enable("false")) multiplexer_1 (
    .in0(sll), .in1(srl), .in2(srr), .in3(rl), .in4(rr), .in5(\and ), .in6(ior), .in7(\xor ), .in8(add),
    .in9(subt), .in10(add), .in11(add), .in12({{22{1'b0}}, sign_comp}), .in13({{22{1'b0}}, unsign_comp}),
    .in14({24{1'b0}}), .in15({24{1'b0}}), .out(ALU_Result), .sel(Operation));
  Shifter #(.width(24), .shift("lr")) shifter_1 (.in(ALU_Source_1), .\dist (bit_extender_1_out), .out(srl));
  Bit_Extender #(.in_width(24), .out_width(5)) bit_extender_1 (.in(ALU_Source_2), .out(bit_extender_1_out));
  assign \and  = ALU_Source_1 & ALU_Source_2;  // AND_Gate and_1, 24 bits wide
  Comparator #(.width(24)) comparator_1 (
    .a(ALU_Source_1), .b(ALU_Source_2), .gt(sign_comp[1]), .eq(sign_comp[0]));  // open: lt
  Bit_Extender #(.in_width(24), .out_width(5)) bit_extender_2 (.in(ALU_Source_2), .out(bit_extender_2_out));
  Shifter #(.width(24), .shift("lr")) shifter_2 (.in(ALU_Source_1), .\dist (bit_extender_2_out), .out(sll));
  Bit_Extender #(.in_width(24), .out_width(5)) bit_extender_3 (.in(ALU_Source_2), .out(bit_extender_3_out));
  assign ior = ALU_Source_1 | ALU_Source_2;  // OR_Gate or_1, 24 bits wide
  Shifter #(.width(24), .shift("ar")) shifter_3 (.in(ALU_Source_1), .\dist (bit_extender_3_out), .out(sra));
  Bit_Extender #(.in_width(24), .out_width(5)) bit_extender_4 (.in(ALU_Source_2), .out(bit_extender_4_out));
  Comparator #(.width(24), .mode("unsigned")) comparator_2 (
    .a(ALU_Source_1), .b(ALU_Source_2), .gt(unsign_comp[1]), .eq(unsign_comp[0]));  // open: lt
  Shifter #(.width(24), .shift("rl")) shifter_4 (.in(ALU_Source_1), .\dist (bit_extender_4_out), .out(rl));
  assign \xor  = ALU_Source_1 ^ ALU_Source_2;  // XOR_Gate xor_1, 24 bits wide
  Shifter #(.width(24), .shift("rr")) shifter_5 (.in(ALU_Source_1), .\dist (bit_extender_5_out), .out(rr));
  Bit_Extender #(.in_width(24), .out_width(5)) bit_extender_5 (.in(ALU_Source_2), .out(bit_extender_5_out));
  Subtractor #(.width(24)) subtractor_1 (.a(ALU_Source_1), .b(ALU_Source_2), .out(subt));  // open: bin, bout
  Adder #(.width(24)) adder_1 (.a(ALU_Source_1), .b(ALU_Source_2), .out(add));  // open: cin, cout

  // Other names for the same wires on the sheet: op[3:0] = Operation; result[23:0] = ALU_Result;
  //   s1[23:0] = ALU_Source_1; s2[23:0] = ALU_Source_2

  // Notes on the sheet:
  //   INPUTS
  //   INPUT PROBES
  //   DO NOT MOVE/ADD/CHANGE ANY INPUT OR OUTPUT PINS!
  //   OUTPUT PROBES
  //   OUTPUT
endmodule
