// Logisim project CPU.circ as structural Verilog: 1 circuit, main circuit Ida CPU
// CPU
module Ida_CPU (
  input  [31:0] Instruction,
  input  Clock,
  output [23:0] Mem_Data,
  output [23:0] Mem_Address,
  output Mem_Write,
  output [23:0] Next_PC,
  output [23:0] r00,
  output [23:0] r01,
  output [23:0] r02,
  output [23:0] r03,
  output [23:0] r04,
  output [23:0] r05,
  output [23:0] r06,
  output [23:0] r07,
  output [23:0] r08,
  output [23:0] r09,
  output [23:0] r10,
  output [23:0] r11,
  output [23:0] r12,
  output [23:0] r13,
  output [23:0] r14,
  output [23:0] r15
);

  wire comparator_1_eq, comparator_2_lt, comparator_3_eq, comparator_6_lt, comparator_7_lt, comparator_8_eq,
       EQ, GT, jump, LT, memRead, multiplexer_2_out, not_1_out, or_1_out, or_2_out, or_3_out, write;
  wire [1:0] bit_extender_1_out, bit_extender_2_out, bit_extender_3_out, cr_q, \type ;
  wire [2:0] CQ__not_used;
  wire [3:0] write_reg;
  wire [23:0] A1, adder_2_out, bit_extender_4_out, bit_extender_5_out, IMM_val, in1, mem_read,
       multiplexer_7_out, pc_q, RI_reg_val, RI_value, RSval, writeval, writeval2;
  wire [31:0] CQin, multiplexer_1_out;
  wire [31:24] CQout;

  // Probe on Instruction
  // Probe on Clock
  // Probe on r00
  // Probe on r01
  // Probe on r02
  // Probe on r03
  // Probe on r04
  // Probe on r05
  // Probe on r06
  // Probe on r07
  not not_1 (not_1_out, EQ);
  // Probe on Mem_Data
  // Probe on Mem_Address
  // Probe on Mem_Write
  // Probe on Next_PC
  Multiplexer #(.width(32), .enable("false")) multiplexer_1 (
    .in0(Instruction), .in1({32{1'b0}}), .out(multiplexer_1_out), .sel(jump));
  Register #(.width(32)) Pipeline_Register (.D(multiplexer_1_out), .Q(CQin), .clk(Clock));  // open: en, clr
  or or_1 (or_1_out, LT, EQ);
  or or_2 (or_2_out, GT, EQ);
  // Probe on r08
  // Probe on r09
  // Probe on r10
  // Probe on r11
  // Probe on r12
  // Probe on r13
  // Probe on r14
  // Probe on r15
  Multiplexer #(.select(3), .enable("false")) multiplexer_2 (
    .in0(1'b0), .in1(or_1_out), .in2(GT), .in3(not_1_out), .in4(EQ), .in5(or_2_out), .in6(LT), .in7(1'b1),
    .out(multiplexer_2_out), .sel(CQin[27:25]));
  Comparator #(.width(4), .mode("unsigned")) comparator_1 (
    .a(CQout[31:28]), .b(4'b1110), .eq(comparator_1_eq));  // open: gt, lt
  Multiplexer #(.width(32), .enable("false")) multiplexer_3 (
    .in0(32'h1000000), .in1(CQin), .out({CQout[31:28], CQ__not_used, CQout[24], A1}), .sel(multiplexer_2_out));
  and and_1 (write, multiplexer_2_out, or_3_out);
  Comparator #(.width(4), .mode("unsigned")) comparator_2 (
    .a(CQout[31:28]), .b(4'b1011), .lt(comparator_2_lt));  // open: gt, eq
  or or_3 (or_3_out, comparator_2_lt, comparator_1_eq);
  Ida_Register_File ida_register_file_1 (
    .Read_Reg_1(A1[19:16]), .Read_Reg_2(IMM_val[3:0]), .Write_Reg(write_reg), .Write_Value(writeval2),
    .Reg_1_Value(RSval), .Reg_2_Value(RI_reg_val), .Reg_Write(write), .Clock(Clock), .r00(r00), .r01(r01),
    .r02(r02), .r03(r03), .r04(r04), .r05(r05), .r06(r06), .r07(r07), .r08(r08), .r09(r09), .r10(r10),
    .r11(r11), .r12(r12), .r13(r13), .r14(r14), .r15(r15), .Reg_3_Value(Mem_Data));
  Ida_ALU ida_alu_1 (.ALU_Source_1(in1), .ALU_Source_2(RI_value), .Operation(CQout[31:28]), .ALU_Result(Mem_Address));
  // Probe on RSval
  // Probe on RI_reg_val
  // Probe on Mem_Data
  // Probe on writeval2
  // Probe on A1[19:16]
  // Probe on IMM_val[3:0]
  // Probe on write_reg
  Multiplexer #(.width(4), .enable("false")) multiplexer_4 (
    .in0(A1[23:20]), .in1(4'b0010), .out(write_reg), .sel(comparator_3_eq));
  Comparator #(.width(4), .mode("unsigned")) comparator_3 (
    .a(CQout[31:28]), .b(4'b1110), .eq(comparator_3_eq));  // open: gt, lt
  Multiplexer #(.width(24), .enable("false")) multiplexer_5 (
    .in0(Mem_Address), .in1(RI_value), .out(writeval), .sel(comparator_3_eq));
  Multiplexer #(.width(24), .enable("false")) multiplexer_6 (
    .in0(writeval), .in1(mem_read), .out(writeval2), .sel(memRead));
  Comparator #(.width(4), .mode("unsigned")) comparator_4 (
    .a(CQout[31:28]), .b(4'b1010), .eq(memRead));  // open: gt, lt
  Comparator #(.width(4), .mode("unsigned")) comparator_5 (
    .a(CQout[31:28]), .b(4'b1011), .eq(Mem_Write));  // open: gt, lt
  Comparator #(.width(4), .mode("unsigned")) comparator_6 (
    .a(CQout[31:28]), .b(4'b1100), .lt(comparator_6_lt));  // open: gt, eq
  assign bit_extender_1_out = {{1{1'b0}}, comparator_6_lt};  // Bit_Extender bit_extender_1
  Comparator #(.width(4), .mode("unsigned")) comparator_7 (
    .a(CQout[31:28]), .b(4'b1110), .lt(comparator_7_lt));  // open: gt, eq
  assign bit_extender_2_out = {{1{1'b0}}, comparator_7_lt};  // Bit_Extender bit_extender_2
  Bit_Extender #(.in_width(24), .out_width(2)) bit_extender_3 (.in(Mem_Address), .out(bit_extender_3_out));
  Comparator #(.width(2), .mode("unsigned")) comparator_8 (
    .a(\type ), .b(2'b01), .eq(comparator_8_eq));  // open: gt, lt
  Adder #(.width(2)) adder_1 (.a(bit_extender_1_out), .b(bit_extender_2_out), .out(\type ));  // open: cin, cout
  Adder #(.width(24)) adder_2 (.a(pc_q), .b(24'h1), .out(adder_2_out));  // open: cin, cout
  Register #(.width(2)) cr (.D(bit_extender_3_out), .en(comparator_8_eq), .Q(cr_q), .clk(Clock));  // open: clr
  RAM #(.addrWidth(24), .dataWidth(24), .bus("separate")) ram_1 (
    .addr(Mem_Address), .din(Mem_Data), .data(mem_read), .str(Mem_Write), .clk(Clock), .ld(memRead));  // open: sel, clr
  Register #(.width(24)) pc (.D(multiplexer_7_out), .Q(pc_q), .clk(Clock));  // open: en, clr
  Multiplexer #(.width(24), .enable("false")) multiplexer_7 (
    .in0(adder_2_out), .in1(Next_PC), .out(multiplexer_7_out), .sel(jump));
  Comparator #(.width(2), .mode("unsigned")) comparator_9 (.a(cr_q), .b(2'b01), .gt(GT), .eq(EQ), .lt(LT));
  Multiplexer #(.select(2), .width(24), .enable("false")) multiplexer_8 (
    .in0({24{1'b0}}), .in1(Mem_Data), .in2(RSval), .out(in1), .sel(\type ));  // open: in3
  Multiplexer #(.width(24), .enable("false")) multiplexer_9 (
    .in0(RI_reg_val), .in1(IMM_val), .out(RI_value), .sel(CQout[24]));
  assign bit_extender_4_out = {{4{1'b0}}, A1[19:0]};  // Bit_Extender bit_extender_4
  assign bit_extender_5_out = {{8{1'b0}}, A1[15:0]};  // Bit_Extender bit_extender_5
  Comparator #(.width(4), .mode("unsigned")) comparator_10 (.a(CQout[31:28]), .b(4'b1111), .eq(jump));  // open: gt, lt
  Multiplexer #(.select(2), .width(24), .enable("false")) multiplexer_10 (
    .in0(A1), .in1(bit_extender_4_out), .in2(bit_extender_5_out), .out(IMM_val), .sel(\type ));  // open: in3
  // Probe on CQout[31:28]
  // Probe on CQ__not_used
  // Probe on A1
  // Probe on IMM_val
  // Probe on A1[15:0]
  // Probe on \type 
  // Probe on RI_value
  Multiplexer #(.width(24), .enable("false")) multiplexer_11 (.in0(pc_q), .in1(RI_value), .out(Next_PC), .sel(jump));

  // Other names for the same wires on the sheet: clk = Clock; A2[19:0] = A1[19:0]; A3[15:0] = A1[15:0];
  //   CQout (some bits) = {CQ__not_used, A1}; RS[3:0] = A1[19:16]; RD[3:0] = A1[23:20]; IMM = CQout[24];
  //   op[3:0] = CQout[31:28]; RI[3:0] = IMM_val[3:0]; inst[31:0] = Instruction; ALUout[23:0] = Mem_Address;
  //   memAddr[23:0] = Mem_Address; memData[23:0] = Mem_Data; RDval[23:0] = Mem_Data; memWrite = Mem_Write;
  //   nextPC[23:0] = Next_PC

  // Notes on the sheet:
  //   INPUTS
  //   INPUT PROBES
  //   OUTPUT PROBES
  //   OUTPUTS
  //   DO NOT MOVE/ADD/CHANGE ANY INPUT OR OUTPUT PINS!
  //   op=14
endmodule
