// Logisim project REG.circ as structural Verilog: 1 circuit, main circuit Ida Register File
// Register File
module Ida_Register_File (
  input  [3:0] Read_Reg_1,
  input  [3:0] Read_Reg_2,
  input  [3:0] Write_Reg,
  input  [23:0] Write_Value,
  input  Reg_Write,
  input  Clock,
  output [23:0] Reg_1_Value,
  output [23:0] Reg_2_Value,
  output [23:0] Reg_3_Value,
  output [23:0] r00,
  output [23:0] r01,
  output [23:0] r02,
  output [23:0] r03,
  output [23:0] r04,
  output [23:0] r05,
  output [23:0] r06,
  output [23:0] r07,
  output [23:0] r08,
  output [23:0] r09,
  output [23:0] r10,
  output [23:0] r11,
  output [23:0] r12,
  output [23:0] r13,
  output [23:0] r14,
  output [23:0] r15
);

  wire or_1_out, or_2_out, or_3_out, or_4_out, or_5_out, or_6_out, or_7_out, or_8_out, or_9_out, or_10_out,
       or_11_out, or_12_out, or_13_out, or_14_out, or_15_out, or_16_out, R00w, R01w, R02w, R03w, R04w, R05w,
       R06w, R07w, R08w, R09w, R10w, R11w, R12w, R13w, R14w, R15w;

  // Probe on Read_Reg_1
  // Probe on Read_Reg_2
  // Probe on Write_Reg
  // Probe on Write_Value
  // Probe on Reg_Write
  // Probe on Clock
  // Probe on Reg_1_Value
  // Probe on Reg_2_Value
  // Probe on Reg_3_Value
  // Probe on r00
  // Probe on r01
  // Probe on r02
  // Probe on r03
  // Probe on r04
  // Probe on r05
  // Probe on r06
  // Probe on r07
  // Probe on r08
  // Probe on r09
  // Probe on r10
  // Probe on r11
  // Probe on r12
  // Probe on r13
  // Probe on r14
  // Probe on r15
  Register #(.width(24)) u_R00 (.D({24{1'b0}}), .en(or_1_out), .Q(r00), .clk(Clock));  // open: clr
  or or_1 (or_1_out, 1'b0, R00w);
  or or_2 (or_2_out, 1'b0, R04w);
  or or_3 (or_3_out, 1'b0, R08w);
  or or_4 (or_4_out, 1'b0, R12w);
  Multiplexer #(.select(4), .width(24), .enable("false")) multiplexer_1 (
    .in0(r00), .in1(r01), .in2(r02), .in3(r03), .in4(r04), .in5(r05), .in6(r06), .in7(r07), .in8(r08),
    .in9(r09), .in10(r10), .in11(r11), .in12(r12), .in13(r13), .in14(r14), .in15(r15), .out(Reg_1_Value),
    .sel(Read_Reg_1));
  Register #(.width(24)) u_R04 (.D(Write_Value), .en(or_2_out), .Q(r04), .clk(Clock));  // open: clr
  Register #(.width(24)) u_R08 (.D(Write_Value), .en(or_3_out), .Q(r08), .clk(Clock));  // open: clr
  Register #(.width(24)) u_R12 (.D(Write_Value), .en(or_4_out), .Q(r12), .clk(Clock));  // open: clr
  or or_5 (or_5_out, 1'b0, R01w);
  or or_6 (or_6_out, 1'b0, R05w);
  or or_7 (or_7_out, 1'b0, R09w);
  or or_8 (or_8_out, 1'b0, R13w);
  Register #(.width(24)) u_R01 (.D(Write_Value), .en(or_5_out), .Q(r01), .clk(Clock));  // open: clr
  Register #(.width(24)) u_R05 (.D(Write_Value), .en(or_6_out), .Q(r05), .clk(Clock));  // open: clr
  Register #(.width(24)) u_R09 (.D(Write_Value), .en(or_7_out), .Q(r09), .clk(Clock));  // open: clr
  Register #(.width(24)) u_R13 (.D(Write_Value), .en(or_8_out), .Q(r13), .clk(Clock));  // open: clr
  Multiplexer #(.select(4), .width(24), .enable("false")) multiplexer_2 (
    .in0(r00), .in1(r01), .in2(r02), .in3(r03), .in4(r04), .in5(r05), .in6(r06), .in7(r07), .in8(r08),
    .in9(r09), .in10(r10), .in11(r11), .in12(r12), .in13(r13), .in14(r14), .in15(r15), .out(Reg_2_Value),
    .sel(Read_Reg_2));
  or or_9 (or_9_out, 1'b0, R02w);
  or or_10 (or_10_out, 1'b0, R06w);
  or or_11 (or_11_out, 1'b0, R10w);
  or or_12 (or_12_out, 1'b0, R14w);
  Register #(.width(24)) u_R02 (.D(Write_Value), .en(or_9_out), .Q(r02), .clk(Clock));  // open: clr
  Register #(.width(24)) u_R06 (.D(Write_Value), .en(or_10_out), .Q(r06), .clk(Clock));  // open: clr
  Register #(.width(24)) u_R10 (.D(Write_Value), .en(or_11_out), .Q(r10), .clk(Clock));  // open: clr
  Register #(.width(24)) u_R14 (.D(Write_Value), .en(or_12_out), .Q(r14), .clk(Clock));  // open: clr
  Multiplexer #(.select(4), .width(24), .enable("false")) multiplexer_3 (
    .in0(r00), .in1(r01), .in2(r02), .in3(r03), .in4(r04), .in5(r05), .in6(r06), .in7(r07), .in8(r08),
    .in9(r09), .in10(r10), .in11(r11), .in12(r12), .in13(r13), .in14(r14), .in15(r15), .out(Reg_3_Value),
    .sel(Write_Reg));
  Register #(.width(24)) u_R03 (.D(Write_Value), .en(or_13_out), .Q(r03), .clk(Clock));  // open: clr
  or or_13 (or_13_out, 1'b0, R03w);
  Register #(.width(24)) u_R07 (.D(Write_Value), .en(or_14_out), .Q(r07), .clk(Clock));  // open: clr
  or or_14 (or_14_out, 1'b0, R07w);
  or or_15 (or_15_out, 1'b0, R11w);
  or or_16 (or_16_out, 1'b0, R15w);
  Register #(.width(24)) u_R11 (.D(Write_Value), .en(or_15_out), .Q(r11), .clk(Clock));  // open: clr
  Register #(.width(24)) u_R15 (.D(Write_Value), .en(or_16_out), .Q(r15), .clk(Clock));  // open: clr
  Demultiplexer #(.select(4), .enable("false")) demultiplexer_1 (
    .out0(R00w), .out1(R01w), .out2(R02w), .out3(R03w), .out4(R04w), .out5(R05w), .out6(R06w), .out7(R07w),
    .out8(R08w), .out9(R09w), .out10(R10w), .out11(R11w), .out12(R12w), .out13(R13w), .out14(R14w),
    .out15(R15w), .in(Reg_Write), .sel(Write_Reg));

  // Other names for the same wires on the sheet: clk = Clock; reg1Read[3:0] = Read_Reg_1; reg1Val[23:0] = Reg_1_Value;
  //   reg2Read[3:0] = Read_Reg_2; reg2Val[23:0] = Reg_2_Value; reg3Val[23:0] = Reg_3_Value;
  //   reg3Write[3:0] = Write_Reg; write = Reg_Write; writeVal[23:0] = Write_Value

  // Notes on the sheet:
  //   INPUT PINS
  //   INPUT PROBES
  //   OUTPUT PROBES
  //   OUTPUT PINS
  //   DO NOT MOVE/ADD/CHANGE ANY INPUT OR OUTPUT PINS!
endmodule
