// Logisim project RUN.circ as structural Verilog: 1 circuit, main circuit Ida CPU Harness
// Harness
module Ida_CPU_Harness (
);

  wire clk, memWrite;
  wire [23:0] memAddr, memData, PC, R00, R01, R02, R03, R04, R05, R06, R07, R08, R09, R10, R11, R12, R13,
       R14, R15;
  wire [31:0] ram_1_data;

  Clock clock_1 (.out(clk));
  // Probe on memData
  // Probe on memAddr
  // Probe on memWrite
  // Probe on PC
  // Probe on R00
  // Probe on R01
  // Probe on R02
  // Probe on R03
  // Probe on R04
  // Probe on R05
  // Probe on R06
  // Probe on R07
  // Probe on R08
  // Probe on R09
  // Probe on R10
  // Probe on R11
  // Probe on R12
  // Probe on R13
  // Probe on R14
  // Probe on R15
  RAM #(.addrWidth(24), .dataWidth(32)) ram_1 (.addr(PC), .data(ram_1_data));  // open: sel, clk, ld, clr
  Ida_CPU ida_cpu_1 (
    .Instruction(ram_1_data), .Clock(clk), .Next_PC(PC), .r00(R00), .r01(R01), .r02(R02), .r03(R03),
    .r04(R04), .r05(R05), .r06(R06), .r07(R07), .r08(R08), .r09(R09), .r10(R10), .r11(R11), .r12(R12),
    .r13(R13), .r14(R14), .r15(R15), .Mem_Data(memData), .Mem_Address(memAddr), .Mem_Write(memWrite));

  // Notes on the sheet:
  //   OUTPUT PROBES
  //   THIS FILE IS USED FOR TESTING. THERE IS NO NEED TO CHANGE IT. IT WILL NOT BE SUBMITTED!
  //   ALSO NOTE THAT THIS FILE WILL *NOT* WORK UNTIL THE ENTIRE PROJECT IS FUNCTIONAL!
endmodule
